# Fritzing sketch wiring pixracer pi zero power (saved by Fritzing 0.9.6b)

parts:
  MCU1 = Raspberry Pi Zero
  JST_GHR_6Pin = Header 6 [package=molex-1x6-ra_lock]
  JST_GHR_4Pin = Header 4 [package=molex-1x4_lock]
  MCU2 = Raspberry Pi Zero
  DHT1 = DHT22 Humidity and Temperature Sensor
  R1 = Resistor [tolerance=±5% resistance=4.7k package="2010 [SMD]"]

nets:
  N1: MCU1.pin_1, DHT1.VDD, R1.Pin_1
  N2: MCU1.pin_2, JST_GHR_4Pin.1
  N3: MCU1.pin_6, MCU1.pin_9, MCU1.pin_14, MCU1.pin_30, JST_GHR_6Pin.6, JST_GHR_4Pin.3, JST_GHR_4Pin.4, MCU2.pin_6, MCU2.pin_14, MCU2.pin_34, DHT1.GND
  N4: MCU1.pin_8, JST_GHR_6Pin.3
  N5: MCU1.pin_10, JST_GHR_6Pin.2, MCU2.pin_10
  N6: MCU1.pin_16, DHT1.DATA, R1.Pin_0
  N7: JST_GHR_4Pin.2, MCU2.pin_2, MCU2.pin_4
